# Fritzing sketch CircuitSketch (saved by Fritzing 0.9.3b)
breadboards: 1

parts:
  U1 = NodeMCU V3.0
  Bauteil1 = Soil Moisture Sensor
  R1 = Resistor [tolerance=±5% resistance=1k package=THT]
  M1 = DC Motor
  Q1 = NPN-Transistor [package="TO92 [THT]"]

nets:
  N1: U1.D0, U1.RST
  N2: U1.D1, R1.Pin_1
  N3: U1.D2, Bauteil1.VCC
  N4: U1.3V3, Q1.C
  N5: U1.GND#6, U1.GND#13, U1.GND#16, U1.GND#33, Bauteil1.GND, M1.pin_1
  N6: U1.A0, Bauteil1.SIG
  N7: R1.Pin_0, Q1.B
  N8: M1.pin_2, Q1.E

notes:
  Waterpump

custom parts:
  NodeMCU V3.0: ESP8266 based NodeMCU
